// Logisim project cpu.circ as structural Verilog: 9 circuits, main circuit main
module main (
  input  reset
);

  wire ALUinB, and_1_out, and_2_out, BGT, BR, clk, decoder_1_out2, decoder_1_out4, decoder_1_out6,
       decoder_1_out9, decoder_1_out10, decoder_1_out12, decoder_1_out13, decoder_1_out14, decoder_1_out15,
       DMwe, JP, Jr, keyboard_1_avail, KRE, LorR, memory_latch_1_oe_latched, memory_latch_1_we_latched, nclk,
       not_3_out, not_4_out, Rdst, Rwd, shifting, success, TTYWe, WE, ZERO;
  wire [1:0] ALUctrl;
  wire [2:0] multiplexer_2_out, multiplexer_4_out;
  wire [6:0] bit_extender_1_out;
  wire [7:0] Kout;
  wire [11:0] address;
  wire [15:0] ALUout, bit_extender_2_out, left_shifter_1_shifted, memory_latch_1_address_latched,
       memory_latch_1_data_in_latched, multiplexer_1_out, multiplexer_3_out, multiplexer_5_out,
       multiplexer_6_out, multiplexer_8_out, multiplexer_9_out, multiplexer_10_out, multiplexer_11_out, PCp1,
       ram_1_dout, regS, regT, right_shifter_1_shifted, shifted, singlereg_1_regout,
       sixteen_bit_adder_2_result;
  wire [15:12] insns;

  SingleReg singlereg_1 (.Reset(reset), .WE(1'b1), .clk(nclk), .RegIn(multiplexer_10_out), .RegOut(singlereg_1_regout));
  ROM #(.addrWidth(16), .dataWidth(16)) rom_1 (.addr(singlereg_1_regout), .data({insns, address}));
  Decoder #(.select(4)) decoder_1 (
    .out0(TTYWe), .out1(KRE), .out2(decoder_1_out2), .out3(Jr), .out4(decoder_1_out4), .out5(BGT),
    .out6(decoder_1_out6), .out7(DMwe), .out8(Rwd), .out9(decoder_1_out9), .out10(decoder_1_out10),
    .out11(LorR), .out12(decoder_1_out12), .out13(decoder_1_out13), .out14(decoder_1_out14),
    .out15(decoder_1_out15), .sel(insns));  // open: en
  sixteen_bit_adder sixteen_bit_adder_1 (.result(PCp1), .B(16'h1), .A(singlereg_1_regout));  // open: ovf, sub
  or or_1 (WE, KRE, decoder_1_out2, Rwd, decoder_1_out9, decoder_1_out10, LorR, decoder_1_out12, decoder_1_out13, decoder_1_out14, decoder_1_out15);
  or or_2 (ALUctrl[1], decoder_1_out9, decoder_1_out10);
  Clock clock_1 (.out(clk));
  not not_1 (nclk, clk);
  or or_3 (ALUctrl[0], BGT, decoder_1_out9, decoder_1_out13);
  or or_4 (Rdst, KRE, Rwd, decoder_1_out14);
  Multiplexer #(.width(16), .enable("false")) multiplexer_1 (
    .in0(multiplexer_3_out), .in1({{8{1'b0}}, Kout}), .out(multiplexer_1_out), .sel(KRE));
  Multiplexer #(.width(3), .enable("false")) multiplexer_2 (
    .in0(address[5:3]), .in1(address[8:6]), .out(multiplexer_2_out), .sel(Rdst));
  or or_5 (ALUinB, DMwe, Rwd, decoder_1_out14);
  Bit_Extender #(.in_width(16), .out_width(7)) bit_extender_1 (.in(regS), .out(bit_extender_1_out));
  Multiplexer #(.width(16), .enable("false")) multiplexer_3 (
    .in0(multiplexer_6_out), .in1(PCp1), .out(multiplexer_3_out), .sel(JP));
  Multiplexer #(.width(3), .enable("false")) multiplexer_4 (
    .in0(multiplexer_2_out), .in1(3'b111), .out(multiplexer_4_out), .sel(JP));
  // Probe on address[5:3]
  or or_6 (shifting, LorR, decoder_1_out12);
  // Probe on address[11:9]
  Keyboard keyboard_1 (.clk(nclk), .re(KRE), .clr(reset), .avail(keyboard_1_avail), .data(Kout[6:0]));
  TTY #(.rows(13), .cols(80)) tty_1 (.data(bit_extender_1_out), .clk(clk), .we(TTYWe), .clr(reset));
  // Probe on address[8:6]
  not not_2 (Kout[7], keyboard_1_avail);
  RegisterFile registerfile_1 (
    .clk(clk), .Reset(reset), .WriteData(multiplexer_1_out), .WriteReg(multiplexer_4_out),
    .ReadReg1(address[11:9]), .ReadReg2(address[8:6]), .RegWriteEnable(WE), .ReadData1(regS), .ReadData2(regT));
  // Probe on address
  or or_7 (BR, decoder_1_out6, BGT);
  Multiplexer #(.width(16), .enable("false")) multiplexer_5 (
    .in0(regT), .in1(bit_extender_2_out), .out(multiplexer_5_out), .sel(ALUinB));
  assign bit_extender_2_out = {{10{address[5]}}, address[5:0]};  // Bit_Extender bit_extender_2
  // Probe on address[5:0]
  not not_3 (not_3_out, ALUout[15]);
  and and_1 (and_1_out, not_3_out, not_4_out);
  not not_4 (not_4_out, ZERO);
  or or_8 (JP, decoder_1_out4, Jr, decoder_1_out2);
  Multiplexer #(.width(16), .enable("false")) multiplexer_6 (
    .in0(multiplexer_11_out), .in1(shifted), .out(multiplexer_6_out), .sel(shifting));
  ALU alu_1 (.OData(ALUout), .opType(ALUctrl), .IData2(multiplexer_5_out), .IData1(regS), .Z(ZERO));
  Multiplexer #(.enable("false")) multiplexer_7 (.in0(ZERO), .in1(and_1_out), .out(success), .sel(BGT));
  sixteen_bit_adder sixteen_bit_adder_2 (
    .result(sixteen_bit_adder_2_result), .B(bit_extender_2_out), .A(PCp1));  // open: ovf, sub
  Multiplexer #(.width(16), .enable("false")) multiplexer_8 (
    .in0(PCp1), .in1(sixteen_bit_adder_2_result), .out(multiplexer_8_out), .sel(and_2_out));
  and and_2 (and_2_out, BR, success);
  RAM #(.addrWidth(16), .dataWidth(16), .trigger("high"), .databus("bibus")) ram_1 (
    .addr(memory_latch_1_address_latched), .we(memory_latch_1_we_latched), .oe(memory_latch_1_oe_latched),
    .din(memory_latch_1_data_in_latched), .dout(ram_1_dout));
  memory_latch memory_latch_1 (
    .address(ALUout), .WE(DMwe), .clk(nclk), .data_in(regT),
    .address_latched(memory_latch_1_address_latched), .WE_latched(memory_latch_1_we_latched),
    .OE_latched(memory_latch_1_oe_latched), .data_in_latched(memory_latch_1_data_in_latched));
  Multiplexer #(.width(16), .enable("false")) multiplexer_9 (
    .in0({4'b0000, address}), .in1(regS), .out(multiplexer_9_out), .sel(Jr));
  Multiplexer #(.width(16), .enable("false")) multiplexer_10 (
    .in0(multiplexer_8_out), .in1(multiplexer_9_out), .out(multiplexer_10_out), .sel(JP));
  left_shifter left_shifter_1 (.num_in(regS), .shamt(address[2:0]), .shifted(left_shifter_1_shifted));
  right_shifter right_shifter_1 (.num_in(regS), .shamt(address[2:0]), .shifted(right_shifter_1_shifted));
  Multiplexer #(.width(16), .enable("false")) multiplexer_11 (
    .in0(ALUout), .in1(ram_1_dout), .out(multiplexer_11_out), .sel(Rwd));
  Multiplexer #(.width(16), .enable("false")) multiplexer_12 (
    .in0(left_shifter_1_shifted), .in1(right_shifter_1_shifted), .out(shifted), .sel(LorR));

  // Other names for the same wires on the sheet: Opcode[3:0] = insns; ALUop[1:0] = ALUctrl; Imm[5:0] = address[5:0];
  //   insns[11:0] = address; jump16[11:0] = address; shamt[2:0] = address[2:0]; Rd[2:0] = address[5:3];
  //   Rt[2:0] = address[8:6]; Rs[2:0] = address[11:9]

  // Notes on the sheet:
  //   R-Type
  //   J-Type
  //   I-Type
  //   output
  //   input
  //   jal
  //   jr
  //   j
  //   bgt
  //   beq
  //   sw
  //   lw
  //   xor
  //   and
  //   srl
  //   sll
  //   sub
  //   addi
  //   add
  //   output
  //   input
  //   jal
  //   jr
  //   j
  //   bgt
  //   beq
  //   sw
  //   lw
  //   xor
  //   and
  //   srl
  //   sll
  //   sub
  //   addi
  //   add
  //   output
  //   input
  //   jal
  //   jr
  //   j
  //   bgt
  //   beq
  //   sw
  //   lw
  //   xor
  //   and
  //   srl
  //   sll
  //   sub
  //   addi
  //   add
endmodule

module RegisterFile (
  input  clk,
  input  Reset,
  input  [15:0] WriteData,
  input  [2:0] WriteReg,
  input  [2:0] ReadReg1,
  input  [2:0] ReadReg2,
  input  RegWriteEnable,
  output [15:0] ReadData1,
  output [15:0] ReadData2
);

  wire and_1_out, and_2_out, and_3_out, and_4_out, and_5_out, and_6_out, and_7_out, e1, e2, e3, e4, e5, e6,
       e7, RE10, RE11, RE12, RE13, RE14, RE15, RE16, RE17, RE20, RE21, RE22, RE23, RE24, RE25, RE26, RE27;
  wire [15:0] o1, o2, o3, o4, o5, o6, o7;

  Decoder #(.select(3)) decoder_1 (
    .out1(e1), .out2(e2), .out3(e3), .out4(e4), .out5(e5), .out6(e6), .out7(e7), .sel(WriteReg));  // open: out0, en
  Decoder #(.select(3)) decoder_2 (
    .out0(RE10), .out1(RE11), .out2(RE12), .out3(RE13), .out4(RE14), .out5(RE15), .out6(RE16), .out7(RE17),
    .sel(ReadReg1));  // open: en
  assign ReadData1 = RE10 ? {16{1'b0}} : 16'bz;  // Controlled_Buffer controlled_buffer_1
  assign ReadData1 = RE11 ? o1 : 16'bz;  // Controlled_Buffer controlled_buffer_2
  assign ReadData1 = RE12 ? o2 : 16'bz;  // Controlled_Buffer controlled_buffer_3
  assign ReadData1 = RE13 ? o3 : 16'bz;  // Controlled_Buffer controlled_buffer_4
  assign ReadData1 = RE14 ? o4 : 16'bz;  // Controlled_Buffer controlled_buffer_5
  assign ReadData1 = RE15 ? o5 : 16'bz;  // Controlled_Buffer controlled_buffer_6
  assign ReadData1 = RE16 ? o6 : 16'bz;  // Controlled_Buffer controlled_buffer_7
  assign ReadData1 = RE17 ? o7 : 16'bz;  // Controlled_Buffer controlled_buffer_8
  Decoder #(.select(3)) decoder_3 (
    .out0(RE20), .out1(RE21), .out2(RE22), .out3(RE23), .out4(RE24), .out5(RE25), .out6(RE26), .out7(RE27),
    .sel(ReadReg2));  // open: en
  assign ReadData2 = RE20 ? {16{1'b0}} : 16'bz;  // Controlled_Buffer controlled_buffer_9
  assign ReadData2 = RE21 ? o1 : 16'bz;  // Controlled_Buffer controlled_buffer_10
  assign ReadData2 = RE22 ? o2 : 16'bz;  // Controlled_Buffer controlled_buffer_11
  assign ReadData2 = RE23 ? o3 : 16'bz;  // Controlled_Buffer controlled_buffer_12
  assign ReadData2 = RE24 ? o4 : 16'bz;  // Controlled_Buffer controlled_buffer_13
  assign ReadData2 = RE25 ? o5 : 16'bz;  // Controlled_Buffer controlled_buffer_14
  assign ReadData2 = RE26 ? o6 : 16'bz;  // Controlled_Buffer controlled_buffer_15
  assign ReadData2 = RE27 ? o7 : 16'bz;  // Controlled_Buffer controlled_buffer_16
  and and_1 (and_1_out, RegWriteEnable, e1);
  and and_2 (and_2_out, RegWriteEnable, e2);
  and and_3 (and_3_out, RegWriteEnable, e3);
  and and_4 (and_4_out, RegWriteEnable, e4);
  and and_5 (and_5_out, RegWriteEnable, e5);
  and and_6 (and_6_out, RegWriteEnable, e6);
  and and_7 (and_7_out, RegWriteEnable, e7);
  // Probe on {16{1'b0}}
  SingleReg singlereg_1 (.Reset(Reset), .WE(and_1_out), .clk(clk), .RegIn(WriteData), .RegOut(o1));
  SingleReg singlereg_2 (.Reset(Reset), .WE(and_2_out), .clk(clk), .RegIn(WriteData), .RegOut(o2));
  SingleReg singlereg_3 (.Reset(Reset), .WE(and_3_out), .clk(clk), .RegIn(WriteData), .RegOut(o3));
  SingleReg singlereg_4 (.Reset(Reset), .WE(and_4_out), .clk(clk), .RegIn(WriteData), .RegOut(o4));
  SingleReg singlereg_5 (.Reset(Reset), .WE(and_5_out), .clk(clk), .RegIn(WriteData), .RegOut(o5));
  SingleReg singlereg_6 (.Reset(Reset), .WE(and_6_out), .clk(clk), .RegIn(WriteData), .RegOut(o6));
  SingleReg singlereg_7 (.Reset(Reset), .WE(and_7_out), .clk(clk), .RegIn(WriteData), .RegOut(o7));
  // Probe on o1
  // Probe on o2
  // Probe on o3
  // Probe on o4
  // Probe on o5
  // Probe on o6
  // Probe on o7
endmodule

module SingleReg (
  input  Reset,
  input  WE,
  input  clk,
  input  [15:0] RegIn,
  output [15:0] RegOut
);

  wire and_1_out, and_2_out, and_3_out, and_4_out, and_5_out, and_6_out, and_7_out, and_8_out, and_9_out,
       and_10_out, and_11_out, and_12_out, and_13_out, and_14_out, and_15_out, and_16_out;

  D_Flip_Flop d_ff_1 (.D(RegIn[0]), .clk(and_1_out), .Q(RegOut[0]), .reset(Reset));  // open: Qn, preset
  and and_1 (and_1_out, clk, WE);
  D_Flip_Flop d_ff_2 (.D(RegIn[8]), .clk(and_2_out), .Q(RegOut[8]), .reset(Reset));  // open: Qn, preset
  and and_2 (and_2_out, clk, WE);
  D_Flip_Flop d_ff_3 (.D(RegIn[1]), .clk(and_3_out), .Q(RegOut[1]), .reset(Reset));  // open: Qn, preset
  and and_3 (and_3_out, clk, WE);
  D_Flip_Flop d_ff_4 (.D(RegIn[9]), .clk(and_4_out), .Q(RegOut[9]), .reset(Reset));  // open: Qn, preset
  and and_4 (and_4_out, clk, WE);
  D_Flip_Flop d_ff_5 (.D(RegIn[2]), .clk(and_5_out), .Q(RegOut[2]), .reset(Reset));  // open: Qn, preset
  and and_5 (and_5_out, clk, WE);
  D_Flip_Flop d_ff_6 (.D(RegIn[10]), .clk(and_6_out), .Q(RegOut[10]), .reset(Reset));  // open: Qn, preset
  and and_6 (and_6_out, clk, WE);
  D_Flip_Flop d_ff_7 (.D(RegIn[3]), .clk(and_7_out), .Q(RegOut[3]), .reset(Reset));  // open: Qn, preset
  and and_7 (and_7_out, clk, WE);
  D_Flip_Flop d_ff_8 (.D(RegIn[11]), .clk(and_8_out), .Q(RegOut[11]), .reset(Reset));  // open: Qn, preset
  and and_8 (and_8_out, clk, WE);
  D_Flip_Flop d_ff_9 (.D(RegIn[4]), .clk(and_9_out), .Q(RegOut[4]), .reset(Reset));  // open: Qn, preset
  and and_9 (and_9_out, clk, WE);
  D_Flip_Flop d_ff_10 (.D(RegIn[12]), .clk(and_10_out), .Q(RegOut[12]), .reset(Reset));  // open: Qn, preset
  and and_10 (and_10_out, clk, WE);
  D_Flip_Flop d_ff_11 (.D(RegIn[5]), .clk(and_11_out), .Q(RegOut[5]), .reset(Reset));  // open: Qn, preset
  and and_11 (and_11_out, clk, WE);
  D_Flip_Flop d_ff_12 (.D(RegIn[13]), .clk(and_12_out), .Q(RegOut[13]), .reset(Reset));  // open: Qn, preset
  and and_12 (and_12_out, clk, WE);
  D_Flip_Flop d_ff_13 (.D(RegIn[6]), .clk(and_13_out), .Q(RegOut[6]), .reset(Reset));  // open: Qn, preset
  and and_13 (and_13_out, clk, WE);
  D_Flip_Flop d_ff_14 (.D(RegIn[14]), .clk(and_14_out), .Q(RegOut[14]), .reset(Reset));  // open: Qn, preset
  and and_14 (and_14_out, clk, WE);
  and and_15 (and_15_out, clk, WE);
  and and_16 (and_16_out, clk, WE);
  D_Flip_Flop d_ff_15 (.D(RegIn[7]), .clk(and_15_out), .Q(RegOut[7]), .reset(Reset));  // open: Qn, preset
  D_Flip_Flop d_ff_16 (.D(RegIn[15]), .clk(and_16_out), .Q(RegOut[15]), .reset(Reset));  // open: Qn, preset

  // Other names for the same wires on the sheet: i0 = RegIn[0]; i1 = RegIn[1]; i2 = RegIn[2]; i3 = RegIn[3];
  //   i4 = RegIn[4]; i5 = RegIn[5]; i6 = RegIn[6]; i7 = RegIn[7]; i8 = RegIn[8]; i9 = RegIn[9]; i10 = RegIn[10];
  //   i11 = RegIn[11]; i12 = RegIn[12]; i13 = RegIn[13]; i14 = RegIn[14]; i15 = RegIn[15]; o0 = RegOut[0];
  //   o1 = RegOut[1]; o2 = RegOut[2]; o3 = RegOut[3]; o4 = RegOut[4]; o5 = RegOut[5]; o6 = RegOut[6]; o7 = RegOut[7];
  //   o8 = RegOut[8]; o9 = RegOut[9]; o10 = RegOut[10]; o11 = RegOut[11]; o12 = RegOut[12]; o13 = RegOut[13];
  //   o14 = RegOut[14]; o15 = RegOut[15]
endmodule

module sixteen_bit_adder (
  input  [15:0] A,
  input  sub,
  input  [15:0] B,
  output ovf,
  output [15:0] result
);

  wire onebit_full_adder_1_cout, onebit_full_adder_2_cout, onebit_full_adder_3_cout,
       onebit_full_adder_4_cout, onebit_full_adder_5_cout, onebit_full_adder_6_cout,
       onebit_full_adder_7_cout, onebit_full_adder_8_cout, onebit_full_adder_9_cout,
       onebit_full_adder_10_cout, onebit_full_adder_11_cout, onebit_full_adder_12_cout,
       onebit_full_adder_13_cout, onebit_full_adder_14_cout, onebit_full_adder_15_cout,
       onebit_full_adder_16_cout, xor_1_out, xor_2_out, xor_3_out, xor_4_out, xor_5_out, xor_6_out,
       xor_7_out, xor_8_out, xor_9_out, xor_10_out, xor_11_out, xor_12_out, xor_13_out, xor_14_out,
       xor_15_out, xor_16_out;

  xor xor_1 (xor_1_out, B[0], sub);
  onebit_full_adder onebit_full_adder_1 (
    .Cin(sub), .a(A[0]), .b(xor_1_out), .Sum(result[0]), .Cout(onebit_full_adder_1_cout));
  xor xor_2 (xor_2_out, B[1], sub);
  onebit_full_adder onebit_full_adder_2 (
    .Cin(onebit_full_adder_1_cout), .a(A[1]), .b(xor_2_out), .Sum(result[1]), .Cout(onebit_full_adder_2_cout));
  xor xor_3 (xor_3_out, B[2], sub);
  onebit_full_adder onebit_full_adder_3 (
    .Cin(onebit_full_adder_2_cout), .a(A[2]), .b(xor_3_out), .Sum(result[2]), .Cout(onebit_full_adder_3_cout));
  xor xor_4 (xor_4_out, B[3], sub);
  onebit_full_adder onebit_full_adder_4 (
    .Cin(onebit_full_adder_3_cout), .a(A[3]), .b(xor_4_out), .Sum(result[3]), .Cout(onebit_full_adder_4_cout));
  xor xor_5 (xor_5_out, B[4], sub);
  onebit_full_adder onebit_full_adder_5 (
    .Cin(onebit_full_adder_4_cout), .a(A[4]), .b(xor_5_out), .Sum(result[4]), .Cout(onebit_full_adder_5_cout));
  xor xor_6 (xor_6_out, B[5], sub);
  onebit_full_adder onebit_full_adder_6 (
    .Cin(onebit_full_adder_5_cout), .a(A[5]), .b(xor_6_out), .Sum(result[5]), .Cout(onebit_full_adder_6_cout));
  xor xor_7 (xor_7_out, B[6], sub);
  onebit_full_adder onebit_full_adder_7 (
    .Cin(onebit_full_adder_6_cout), .a(A[6]), .b(xor_7_out), .Sum(result[6]), .Cout(onebit_full_adder_7_cout));
  xor xor_8 (xor_8_out, B[7], sub);
  onebit_full_adder onebit_full_adder_8 (
    .Cin(onebit_full_adder_7_cout), .a(A[7]), .b(xor_8_out), .Sum(result[7]), .Cout(onebit_full_adder_8_cout));
  xor xor_9 (xor_9_out, B[8], sub);
  onebit_full_adder onebit_full_adder_9 (
    .Cin(onebit_full_adder_8_cout), .a(A[8]), .b(xor_9_out), .Sum(result[8]), .Cout(onebit_full_adder_9_cout));
  xor xor_10 (xor_10_out, B[9], sub);
  onebit_full_adder onebit_full_adder_10 (
    .Cin(onebit_full_adder_9_cout), .a(A[9]), .b(xor_10_out), .Sum(result[9]),
    .Cout(onebit_full_adder_10_cout));
  xor xor_11 (xor_11_out, B[10], sub);
  onebit_full_adder onebit_full_adder_11 (
    .Cin(onebit_full_adder_10_cout), .a(A[10]), .b(xor_11_out), .Sum(result[10]),
    .Cout(onebit_full_adder_11_cout));
  xor xor_12 (xor_12_out, B[11], sub);
  onebit_full_adder onebit_full_adder_12 (
    .Cin(onebit_full_adder_11_cout), .a(A[11]), .b(xor_12_out), .Sum(result[11]),
    .Cout(onebit_full_adder_12_cout));
  xor xor_13 (xor_13_out, B[12], sub);
  onebit_full_adder onebit_full_adder_13 (
    .Cin(onebit_full_adder_12_cout), .a(A[12]), .b(xor_13_out), .Sum(result[12]),
    .Cout(onebit_full_adder_13_cout));
  xor xor_14 (xor_14_out, B[13], sub);
  onebit_full_adder onebit_full_adder_14 (
    .Cin(onebit_full_adder_13_cout), .a(A[13]), .b(xor_14_out), .Sum(result[13]),
    .Cout(onebit_full_adder_14_cout));
  xor xor_15 (xor_15_out, B[14], sub);
  onebit_full_adder onebit_full_adder_15 (
    .Cin(onebit_full_adder_14_cout), .a(A[14]), .b(xor_15_out), .Sum(result[14]),
    .Cout(onebit_full_adder_15_cout));
  xor xor_16 (xor_16_out, B[15], sub);
  xor xor_17 (ovf, onebit_full_adder_15_cout, onebit_full_adder_16_cout);
  onebit_full_adder onebit_full_adder_16 (
    .Cin(onebit_full_adder_15_cout), .a(A[15]), .b(xor_16_out), .Sum(result[15]),
    .Cout(onebit_full_adder_16_cout));

  // Other names for the same wires on the sheet: a1 = A[0]; a2 = A[1]; a3 = A[2]; a4 = A[3]; a5 = A[4]; a6 = A[5];
  //   a7 = A[6]; a8 = A[7]; a9 = A[8]; a10 = A[9]; a11 = A[10]; a12 = A[11]; a13 = A[12]; a14 = A[13]; a15 = A[14];
  //   a16 = A[15]; b1 = B[0]; b2 = B[1]; b3 = B[2]; b4 = B[3]; b5 = B[4]; b6 = B[5]; b7 = B[6]; b8 = B[7]; b9 = B[8];
  //   b10 = B[9]; b11 = B[10]; b12 = B[11]; b13 = B[12]; b14 = B[13]; b15 = B[14]; b16 = B[15]
endmodule

module ALU (
  input  [15:0] IData1,
  input  [15:0] IData2,
  input  [1:0] opType,
  output [15:0] OData,
  output Z
);

  wire or_1_out;
  wire [15:0] AddOut, and_1_out, SubOut, xor_1_out;

  sixteen_bit_adder sixteen_bit_adder_1 (.result(AddOut), .B(IData2), .A(IData1));  // open: ovf, sub
  sixteen_bit_adder sixteen_bit_adder_2 (.result(SubOut), .B(IData2), .sub(1'b1), .A(IData1));  // open: ovf
  assign and_1_out = IData1 & IData2;  // AND_Gate and_1, 16 bits wide
  assign xor_1_out = IData1 ^ IData2;  // XOR_Gate xor_1, 16 bits wide
  Multiplexer #(.select(2), .width(16), .enable("false")) multiplexer_1 (
    .in0(AddOut), .in1(SubOut), .in2(and_1_out), .in3(xor_1_out), .out(OData), .sel(opType));
  or or_1 (or_1_out, SubOut[0], SubOut[1], SubOut[2], SubOut[3], SubOut[4], SubOut[5], SubOut[6], SubOut[7], SubOut[8], SubOut[9], SubOut[10], SubOut[11], SubOut[12], SubOut[13], SubOut[14], SubOut[15]);
  not not_1 (Z, or_1_out);

  // Other names for the same wires on the sheet: ALUop[1:0] = opType; I1[15:0] = IData1; I2[15:0] = IData2
endmodule

module onebit_full_adder (
  input  Cin,
  input  a,
  input  b,
  output Sum,
  output Cout
);

  wire and_1_out, and_2_out, xor_1_out;

  and and_1 (and_1_out, b, a);
  xor xor_1 (xor_1_out, a, b);
  or or_1 (Cout, and_1_out, and_2_out);
  and and_2 (and_2_out, xor_1_out, Cin);
  xor xor_2 (Sum, Cin, xor_1_out);
endmodule

module memory_latch (
  input  [15:0] address,
  input  WE,
  input  clk,
  input  [15:0] data_in,
  output [15:0] address_latched,
  output WE_latched,
  output OE_latched,
  output [15:0] data_in_latched
);

  wire DMwe_latch_q;
  wire [15:0] addr_latch_q;

  Register #(.width(16), .trigger("falling")) addr_latch (
    .D(address), .en(WE), .clk(clk), .Q(addr_latch_q));  // open: clr
  D_Flip_Flop #(.trigger("falling")) DMwe_latch (.D(WE), .clk(clk), .Q(DMwe_latch_q));  // open: Qn, preset, reset
  Register #(.width(16), .trigger("falling")) data_to_be_written (
    .D(data_in), .en(WE), .clk(clk), .Q(data_in_latched));  // open: clr
  Multiplexer #(.width(16), .enable("false")) multiplexer_1 (
    .in0(address), .in1(addr_latch_q), .out(address_latched), .sel(DMwe_latch_q));
  and and_1 (WE_latched, clk, DMwe_latch_q);
  not not_1 (OE_latched, WE_latched);
endmodule

module left_shifter (
  input  [15:0] num_in,
  input  [2:0] shamt,
  output [15:0] shifted
);

  wire multiplexer_1_out, multiplexer_2_out, multiplexer_3_out, multiplexer_4_out, multiplexer_5_out,
       multiplexer_6_out, multiplexer_7_out, multiplexer_8_out, multiplexer_9_out, multiplexer_10_out,
       multiplexer_11_out, multiplexer_12_out, multiplexer_13_out, multiplexer_14_out, multiplexer_15_out,
       multiplexer_16_out, multiplexer_17_out, multiplexer_18_out, multiplexer_19_out, multiplexer_20_out,
       multiplexer_21_out, multiplexer_22_out, multiplexer_23_out, multiplexer_24_out, multiplexer_25_out,
       multiplexer_26_out, multiplexer_27_out, multiplexer_29_out, multiplexer_30_out, multiplexer_31_out,
       multiplexer_32_out, multiplexer_33_out;

  Multiplexer #(.enable("false")) multiplexer_1 (
    .in0(num_in[15]), .in1(num_in[14]), .out(multiplexer_1_out), .sel(shamt[0]));
  Multiplexer #(.enable("false")) multiplexer_2 (
    .in0(num_in[14]), .in1(num_in[13]), .out(multiplexer_2_out), .sel(shamt[0]));
  Multiplexer #(.enable("false")) multiplexer_3 (
    .in0(num_in[13]), .in1(num_in[12]), .out(multiplexer_3_out), .sel(shamt[0]));
  Multiplexer #(.enable("false")) multiplexer_4 (
    .in0(num_in[12]), .in1(num_in[11]), .out(multiplexer_4_out), .sel(shamt[0]));
  Multiplexer #(.enable("false")) multiplexer_5 (
    .in0(num_in[11]), .in1(num_in[10]), .out(multiplexer_5_out), .sel(shamt[0]));
  Multiplexer #(.enable("false")) multiplexer_6 (
    .in0(num_in[10]), .in1(num_in[9]), .out(multiplexer_6_out), .sel(shamt[0]));
  Multiplexer #(.enable("false")) multiplexer_7 (
    .in0(num_in[9]), .in1(num_in[8]), .out(multiplexer_7_out), .sel(shamt[0]));
  Multiplexer #(.enable("false")) multiplexer_8 (
    .in0(num_in[8]), .in1(num_in[7]), .out(multiplexer_8_out), .sel(shamt[0]));
  Multiplexer #(.enable("false")) multiplexer_9 (
    .in0(num_in[7]), .in1(num_in[6]), .out(multiplexer_9_out), .sel(shamt[0]));
  Multiplexer #(.enable("false")) multiplexer_10 (
    .in0(num_in[6]), .in1(num_in[5]), .out(multiplexer_10_out), .sel(shamt[0]));
  Multiplexer #(.enable("false")) multiplexer_11 (
    .in0(num_in[5]), .in1(num_in[4]), .out(multiplexer_11_out), .sel(shamt[0]));
  Multiplexer #(.enable("false")) multiplexer_12 (
    .in0(multiplexer_1_out), .in1(multiplexer_3_out), .out(multiplexer_12_out), .sel(shamt[1]));
  Multiplexer #(.enable("false")) multiplexer_13 (
    .in0(multiplexer_2_out), .in1(multiplexer_4_out), .out(multiplexer_13_out), .sel(shamt[1]));
  Multiplexer #(.enable("false")) multiplexer_14 (
    .in0(multiplexer_3_out), .in1(multiplexer_5_out), .out(multiplexer_14_out), .sel(shamt[1]));
  Multiplexer #(.enable("false")) multiplexer_15 (
    .in0(num_in[4]), .in1(num_in[3]), .out(multiplexer_15_out), .sel(shamt[0]));
  Multiplexer #(.enable("false")) multiplexer_16 (
    .in0(num_in[3]), .in1(num_in[2]), .out(multiplexer_16_out), .sel(shamt[0]));
  Multiplexer #(.enable("false")) multiplexer_17 (
    .in0(num_in[2]), .in1(num_in[1]), .out(multiplexer_17_out), .sel(shamt[0]));
  Multiplexer #(.enable("false")) multiplexer_18 (
    .in0(num_in[1]), .in1(num_in[0]), .out(multiplexer_18_out), .sel(shamt[0]));
  Multiplexer #(.enable("false")) multiplexer_19 (
    .in0(num_in[0]), .in1(1'b0), .out(multiplexer_19_out), .sel(shamt[0]));
  Multiplexer #(.enable("false")) multiplexer_20 (
    .in0(multiplexer_4_out), .in1(multiplexer_6_out), .out(multiplexer_20_out), .sel(shamt[1]));
  Multiplexer #(.enable("false")) multiplexer_21 (
    .in0(multiplexer_5_out), .in1(multiplexer_7_out), .out(multiplexer_21_out), .sel(shamt[1]));
  Multiplexer #(.enable("false")) multiplexer_22 (
    .in0(multiplexer_6_out), .in1(multiplexer_8_out), .out(multiplexer_22_out), .sel(shamt[1]));
  Multiplexer #(.enable("false")) multiplexer_23 (
    .in0(multiplexer_7_out), .in1(multiplexer_9_out), .out(multiplexer_23_out), .sel(shamt[1]));
  Multiplexer #(.enable("false")) multiplexer_24 (
    .in0(multiplexer_8_out), .in1(multiplexer_10_out), .out(multiplexer_24_out), .sel(shamt[1]));
  Multiplexer #(.enable("false")) multiplexer_25 (
    .in0(multiplexer_9_out), .in1(multiplexer_11_out), .out(multiplexer_25_out), .sel(shamt[1]));
  Multiplexer #(.enable("false")) multiplexer_26 (
    .in0(multiplexer_10_out), .in1(multiplexer_15_out), .out(multiplexer_26_out), .sel(shamt[1]));
  Multiplexer #(.enable("false")) multiplexer_27 (
    .in0(multiplexer_11_out), .in1(multiplexer_16_out), .out(multiplexer_27_out), .sel(shamt[1]));
  Multiplexer #(.enable("false")) multiplexer_28 (
    .in0(multiplexer_12_out), .in1(multiplexer_21_out), .out(shifted[15]), .sel(shamt[2]));
  Multiplexer #(.enable("false")) multiplexer_29 (
    .in0(multiplexer_15_out), .in1(multiplexer_17_out), .out(multiplexer_29_out), .sel(shamt[1]));
  Multiplexer #(.enable("false")) multiplexer_30 (
    .in0(multiplexer_16_out), .in1(multiplexer_18_out), .out(multiplexer_30_out), .sel(shamt[1]));
  Multiplexer #(.enable("false")) multiplexer_31 (
    .in0(multiplexer_17_out), .in1(multiplexer_19_out), .out(multiplexer_31_out), .sel(shamt[1]));
  Multiplexer #(.enable("false")) multiplexer_32 (
    .in0(multiplexer_18_out), .in1(1'b0), .out(multiplexer_32_out), .sel(shamt[1]));
  Multiplexer #(.enable("false")) multiplexer_33 (
    .in0(multiplexer_19_out), .in1(1'b0), .out(multiplexer_33_out), .sel(shamt[1]));
  Multiplexer #(.enable("false")) multiplexer_34 (
    .in0(multiplexer_13_out), .in1(multiplexer_22_out), .out(shifted[14]), .sel(shamt[2]));
  Multiplexer #(.enable("false")) multiplexer_35 (
    .in0(multiplexer_14_out), .in1(multiplexer_23_out), .out(shifted[13]), .sel(shamt[2]));
  Multiplexer #(.enable("false")) multiplexer_36 (
    .in0(multiplexer_20_out), .in1(multiplexer_24_out), .out(shifted[12]), .sel(shamt[2]));
  Multiplexer #(.enable("false")) multiplexer_37 (
    .in0(multiplexer_21_out), .in1(multiplexer_25_out), .out(shifted[11]), .sel(shamt[2]));
  Multiplexer #(.enable("false")) multiplexer_38 (
    .in0(multiplexer_22_out), .in1(multiplexer_26_out), .out(shifted[10]), .sel(shamt[2]));
  Multiplexer #(.enable("false")) multiplexer_39 (
    .in0(multiplexer_23_out), .in1(multiplexer_27_out), .out(shifted[9]), .sel(shamt[2]));
  Multiplexer #(.enable("false")) multiplexer_40 (
    .in0(multiplexer_24_out), .in1(multiplexer_29_out), .out(shifted[8]), .sel(shamt[2]));
  Multiplexer #(.enable("false")) multiplexer_41 (
    .in0(multiplexer_25_out), .in1(multiplexer_30_out), .out(shifted[7]), .sel(shamt[2]));
  Multiplexer #(.enable("false")) multiplexer_42 (
    .in0(multiplexer_26_out), .in1(multiplexer_31_out), .out(shifted[6]), .sel(shamt[2]));
  Multiplexer #(.enable("false")) multiplexer_43 (
    .in0(multiplexer_27_out), .in1(multiplexer_32_out), .out(shifted[5]), .sel(shamt[2]));
  Multiplexer #(.enable("false")) multiplexer_44 (
    .in0(multiplexer_29_out), .in1(multiplexer_33_out), .out(shifted[4]), .sel(shamt[2]));
  Multiplexer #(.enable("false")) multiplexer_45 (
    .in0(multiplexer_30_out), .in1(1'b0), .out(shifted[3]), .sel(shamt[2]));
  Multiplexer #(.enable("false")) multiplexer_46 (
    .in0(multiplexer_31_out), .in1(1'b0), .out(shifted[2]), .sel(shamt[2]));
  Multiplexer #(.enable("false")) multiplexer_47 (
    .in0(multiplexer_32_out), .in1(1'b0), .out(shifted[1]), .sel(shamt[2]));
  Multiplexer #(.enable("false")) multiplexer_48 (
    .in0(multiplexer_33_out), .in1(1'b0), .out(shifted[0]), .sel(shamt[2]));

  // Other names for the same wires on the sheet: i0 = num_in[0]; i1 = num_in[1]; i2 = num_in[2]; i3 = num_in[3];
  //   i4 = num_in[4]; i5 = num_in[5]; i6 = num_in[6]; i7 = num_in[7]; i8 = num_in[8]; i9 = num_in[9];
  //   i10 = num_in[10]; i11 = num_in[11]; i12 = num_in[12]; i13 = num_in[13]; i14 = num_in[14]; i15 = num_in[15];
  //   s0 = shamt[0]; s1 = shamt[1]; s2 = shamt[2]; o0 = shifted[0]; o1 = shifted[1]; o2 = shifted[2]; o3 = shifted[3];
  //   o4 = shifted[4]; o5 = shifted[5]; o6 = shifted[6]; o7 = shifted[7]; o8 = shifted[8]; o9 = shifted[9];
  //   o10 = shifted[10]; o11 = shifted[11]; o12 = shifted[12]; o13 = shifted[13]; o14 = shifted[14];
  //   o15 = shifted[15]
endmodule

module right_shifter (
  input  [15:0] num_in,
  input  [2:0] shamt,
  output [15:0] shifted
);

  wire multiplexer_1_out, multiplexer_2_out, multiplexer_3_out, multiplexer_4_out, multiplexer_5_out,
       multiplexer_6_out, multiplexer_7_out, multiplexer_8_out, multiplexer_9_out, multiplexer_10_out,
       multiplexer_11_out, multiplexer_12_out, multiplexer_13_out, multiplexer_14_out, multiplexer_15_out,
       multiplexer_16_out, multiplexer_17_out, multiplexer_18_out, multiplexer_19_out, multiplexer_20_out,
       multiplexer_21_out, multiplexer_22_out, multiplexer_23_out, multiplexer_24_out, multiplexer_25_out,
       multiplexer_26_out, multiplexer_27_out, multiplexer_28_out, multiplexer_29_out, multiplexer_30_out,
       multiplexer_31_out, multiplexer_32_out, s0, s1, s2;

  not not_1 (s0, shamt[0]);
  not not_2 (s1, shamt[1]);
  not not_3 (s2, shamt[2]);
  Multiplexer #(.enable("false")) multiplexer_1 (.in0(1'b0), .in1(num_in[15]), .out(multiplexer_1_out), .sel(s0));
  Multiplexer #(.enable("false")) multiplexer_2 (.in0(num_in[15]), .in1(num_in[14]), .out(multiplexer_2_out), .sel(s0));
  Multiplexer #(.enable("false")) multiplexer_3 (.in0(num_in[14]), .in1(num_in[13]), .out(multiplexer_3_out), .sel(s0));
  Multiplexer #(.enable("false")) multiplexer_4 (.in0(num_in[13]), .in1(num_in[12]), .out(multiplexer_4_out), .sel(s0));
  Multiplexer #(.enable("false")) multiplexer_5 (.in0(num_in[12]), .in1(num_in[11]), .out(multiplexer_5_out), .sel(s0));
  Multiplexer #(.enable("false")) multiplexer_6 (.in0(num_in[11]), .in1(num_in[10]), .out(multiplexer_6_out), .sel(s0));
  Multiplexer #(.enable("false")) multiplexer_7 (.in0(num_in[10]), .in1(num_in[9]), .out(multiplexer_7_out), .sel(s0));
  Multiplexer #(.enable("false")) multiplexer_8 (.in0(num_in[9]), .in1(num_in[8]), .out(multiplexer_8_out), .sel(s0));
  Multiplexer #(.enable("false")) multiplexer_9 (.in0(num_in[8]), .in1(num_in[7]), .out(multiplexer_9_out), .sel(s0));
  Multiplexer #(.enable("false")) multiplexer_10 (.in0(num_in[7]), .in1(num_in[6]), .out(multiplexer_10_out), .sel(s0));
  Multiplexer #(.enable("false")) multiplexer_11 (.in0(num_in[6]), .in1(num_in[5]), .out(multiplexer_11_out), .sel(s0));
  Multiplexer #(.enable("false")) multiplexer_12 (.in0(num_in[5]), .in1(num_in[4]), .out(multiplexer_12_out), .sel(s0));
  Multiplexer #(.enable("false")) multiplexer_13 (.in0(num_in[4]), .in1(num_in[3]), .out(multiplexer_13_out), .sel(s0));
  Multiplexer #(.enable("false")) multiplexer_14 (.in0(num_in[3]), .in1(num_in[2]), .out(multiplexer_14_out), .sel(s0));
  Multiplexer #(.enable("false")) multiplexer_15 (.in0(num_in[2]), .in1(num_in[1]), .out(multiplexer_15_out), .sel(s0));
  Multiplexer #(.enable("false")) multiplexer_16 (.in0(num_in[1]), .in1(num_in[0]), .out(multiplexer_16_out), .sel(s0));
  Multiplexer #(.enable("false")) multiplexer_17 (
    .in0(1'b0), .in1(multiplexer_1_out), .out(multiplexer_17_out), .sel(s1));
  Multiplexer #(.enable("false")) multiplexer_18 (
    .in0(1'b0), .in1(multiplexer_2_out), .out(multiplexer_18_out), .sel(s1));
  Multiplexer #(.enable("false")) multiplexer_19 (
    .in0(multiplexer_1_out), .in1(multiplexer_3_out), .out(multiplexer_19_out), .sel(s1));
  Multiplexer #(.enable("false")) multiplexer_20 (
    .in0(multiplexer_2_out), .in1(multiplexer_4_out), .out(multiplexer_20_out), .sel(s1));
  Multiplexer #(.enable("false")) multiplexer_21 (
    .in0(multiplexer_3_out), .in1(multiplexer_5_out), .out(multiplexer_21_out), .sel(s1));
  Multiplexer #(.enable("false")) multiplexer_22 (
    .in0(multiplexer_4_out), .in1(multiplexer_6_out), .out(multiplexer_22_out), .sel(s1));
  Multiplexer #(.enable("false")) multiplexer_23 (
    .in0(multiplexer_5_out), .in1(multiplexer_7_out), .out(multiplexer_23_out), .sel(s1));
  Multiplexer #(.enable("false")) multiplexer_24 (
    .in0(multiplexer_6_out), .in1(multiplexer_8_out), .out(multiplexer_24_out), .sel(s1));
  Multiplexer #(.enable("false")) multiplexer_25 (
    .in0(multiplexer_7_out), .in1(multiplexer_9_out), .out(multiplexer_25_out), .sel(s1));
  Multiplexer #(.enable("false")) multiplexer_26 (
    .in0(multiplexer_8_out), .in1(multiplexer_10_out), .out(multiplexer_26_out), .sel(s1));
  Multiplexer #(.enable("false")) multiplexer_27 (
    .in0(multiplexer_9_out), .in1(multiplexer_11_out), .out(multiplexer_27_out), .sel(s1));
  Multiplexer #(.enable("false")) multiplexer_28 (
    .in0(multiplexer_10_out), .in1(multiplexer_12_out), .out(multiplexer_28_out), .sel(s1));
  Multiplexer #(.enable("false")) multiplexer_29 (
    .in0(multiplexer_11_out), .in1(multiplexer_13_out), .out(multiplexer_29_out), .sel(s1));
  Multiplexer #(.enable("false")) multiplexer_30 (
    .in0(multiplexer_12_out), .in1(multiplexer_14_out), .out(multiplexer_30_out), .sel(s1));
  Multiplexer #(.enable("false")) multiplexer_31 (
    .in0(multiplexer_13_out), .in1(multiplexer_15_out), .out(multiplexer_31_out), .sel(s1));
  Multiplexer #(.enable("false")) multiplexer_32 (
    .in0(multiplexer_14_out), .in1(multiplexer_16_out), .out(multiplexer_32_out), .sel(s1));
  Multiplexer #(.enable("false")) multiplexer_33 (.in0(1'b0), .in1(multiplexer_17_out), .out(shifted[15]), .sel(s2));
  Multiplexer #(.enable("false")) multiplexer_34 (.in0(1'b0), .in1(multiplexer_18_out), .out(shifted[14]), .sel(s2));
  Multiplexer #(.enable("false")) multiplexer_35 (.in0(1'b0), .in1(multiplexer_19_out), .out(shifted[13]), .sel(s2));
  Multiplexer #(.enable("false")) multiplexer_36 (.in0(1'b0), .in1(multiplexer_20_out), .out(shifted[12]), .sel(s2));
  Multiplexer #(.enable("false")) multiplexer_37 (
    .in0(multiplexer_17_out), .in1(multiplexer_21_out), .out(shifted[11]), .sel(s2));
  Multiplexer #(.enable("false")) multiplexer_38 (
    .in0(multiplexer_18_out), .in1(multiplexer_22_out), .out(shifted[10]), .sel(s2));
  Multiplexer #(.enable("false")) multiplexer_39 (
    .in0(multiplexer_19_out), .in1(multiplexer_23_out), .out(shifted[9]), .sel(s2));
  Multiplexer #(.enable("false")) multiplexer_40 (
    .in0(multiplexer_20_out), .in1(multiplexer_24_out), .out(shifted[8]), .sel(s2));
  Multiplexer #(.enable("false")) multiplexer_41 (
    .in0(multiplexer_21_out), .in1(multiplexer_25_out), .out(shifted[7]), .sel(s2));
  Multiplexer #(.enable("false")) multiplexer_42 (
    .in0(multiplexer_22_out), .in1(multiplexer_26_out), .out(shifted[6]), .sel(s2));
  Multiplexer #(.enable("false")) multiplexer_43 (
    .in0(multiplexer_23_out), .in1(multiplexer_27_out), .out(shifted[5]), .sel(s2));
  Multiplexer #(.enable("false")) multiplexer_44 (
    .in0(multiplexer_24_out), .in1(multiplexer_28_out), .out(shifted[4]), .sel(s2));
  Multiplexer #(.enable("false")) multiplexer_45 (
    .in0(multiplexer_25_out), .in1(multiplexer_29_out), .out(shifted[3]), .sel(s2));
  Multiplexer #(.enable("false")) multiplexer_46 (
    .in0(multiplexer_26_out), .in1(multiplexer_30_out), .out(shifted[2]), .sel(s2));
  Multiplexer #(.enable("false")) multiplexer_47 (
    .in0(multiplexer_27_out), .in1(multiplexer_31_out), .out(shifted[1]), .sel(s2));
  Multiplexer #(.enable("false")) multiplexer_48 (
    .in0(multiplexer_28_out), .in1(multiplexer_32_out), .out(shifted[0]), .sel(s2));

  // Other names for the same wires on the sheet: i0 = num_in[0]; i1 = num_in[1]; i2 = num_in[2]; i3 = num_in[3];
  //   i4 = num_in[4]; i5 = num_in[5]; i6 = num_in[6]; i7 = num_in[7]; i8 = num_in[8]; i9 = num_in[9];
  //   i10 = num_in[10]; i11 = num_in[11]; i12 = num_in[12]; i13 = num_in[13]; i14 = num_in[14]; i15 = num_in[15];
  //   o0 = shifted[0]; o1 = shifted[1]; o2 = shifted[2]; o3 = shifted[3]; o4 = shifted[4]; o5 = shifted[5];
  //   o6 = shifted[6]; o7 = shifted[7]; o8 = shifted[8]; o9 = shifted[9]; o10 = shifted[10]; o11 = shifted[11];
  //   o12 = shifted[12]; o13 = shifted[13]; o14 = shifted[14]; o15 = shifted[15]
endmodule
